// Logisim project 8085.circ as structural Verilog: 5 circuits, main circuit main
module main (
  input  [3:0] Din,
  input  [1:0] SetID,
  input  WMem,
  input  Wac,
  input  WALU,
  input  [2:0] WAR,
  input  [2:0] SetAR,
  input  [2:0] SetOP,
  input  Winst,
  input  [15:0] DirIn,
  input  WDR,
  input  WPC,
  input  SetDir,
  input  [1:0] SetIncr,
  output [3:0] Dout,
  output [3:0] MonitorDo_AR
);

  wire CLK_out, undriven;
  wire [3:0] Ac_q, chips_de_memoria_1_dout, multiplexer_2_out;
  wire [15:0] adder_1_out, multiplexer_1_out, multiplexer_3_out, PreCounter_q, RegClr_q;

  Clock CLK (.out(CLK_out));
  Register #(.width(16)) RegClr (.D(multiplexer_3_out), .en(WDR), .Q(RegClr_q), .clk(CLK_out));  // open: clr
  Multiplexer #(.select(2), .width(16), .enable("false")) multiplexer_1 (
    .in1(16'h1), .in2(16'h2), .in3(16'h3), .out(multiplexer_1_out), .sel(SetIncr));  // open: in0
  Chips_de_memoria chips_de_memoria_1 (
    .A(RegClr_q), .R_W(WMem), .DIN(multiplexer_2_out), .CLK(CLK_out), .DOUT(chips_de_memoria_1_dout));
  Adder #(.width(16)) adder_1 (.a(RegClr_q), .b(multiplexer_1_out), .out(adder_1_out));  // open: cin, cout
  Register #(.width(4)) Instuction (.D(multiplexer_2_out), .en(Winst), .clk(CLK_out));  // open: Q, clr
  Register #(.width(16)) PreCounter (.D(adder_1_out), .en(WPC), .Q(PreCounter_q), .clk(CLK_out));  // open: clr
  Multiplexer #(.select(2), .width(4), .enable("false")) multiplexer_2 (
    .in0(Din), .in1(chips_de_memoria_1_dout), .in2(Dout), .in3(MonitorDo_AR), .out(multiplexer_2_out),
    .sel(SetID));
  ARR_T_4B arr_t_4b_1 (.Din(Din), .W(WAR), .Clk(CLK_out), .Set(SetAR), .Dout(MonitorDo_AR));
  Multiplexer #(.width(16), .enable("false")) multiplexer_3 (
    .in0(PreCounter_q), .in1(DirIn), .out(multiplexer_3_out), .sel(SetDir));
  Register #(.width(4)) Ac (.D(multiplexer_2_out), .en(undriven), .Q(Ac_q), .clk(CLK_out));  // open: clr
  ALU_T_4op1r alu_t_4op1r_1 (
    .Acin(Ac_q), .ALUin(MonitorDo_AR), .WALU(WALU), .CLK(CLK_out), .SetOp(SetOP), .ALUout(Dout));

  // Notes on the sheet:
  //   González Robles David Alejandro
endmodule

// AR
module ARR_T_4B (
  input  [3:0] Din,
  input  Clk,
  input  [2:0] W,
  input  [2:0] Set,
  output [3:0] Dout
);

  wire decoder_1_out0, decoder_1_out1, decoder_1_out2, decoder_1_out3, decoder_1_out4, decoder_1_out5,
       decoder_2_out0, decoder_2_out1, decoder_2_out2, decoder_2_out3, decoder_2_out4, decoder_2_out5,
       decoder_2_out6;
  wire [3:0] B_q, C_q, D_q, E_q, F_q, G_q;

  Decoder #(.select(3), .enable("false")) decoder_1 (
    .out0(decoder_1_out0), .out1(decoder_1_out1), .out2(decoder_1_out2), .out3(decoder_1_out3),
    .out4(decoder_1_out4), .out5(decoder_1_out5), .sel(W));  // open: out6, out7
  Register #(.width(4)) B (.D(Din), .en(decoder_1_out0), .Q(B_q), .clk(Clk));  // open: clr
  Register #(.width(4)) C (.D(Din), .en(decoder_1_out1), .Q(C_q), .clk(Clk));  // open: clr
  Register #(.width(4)) D (.D(Din), .en(decoder_1_out2), .Q(D_q), .clk(Clk));  // open: clr
  Register #(.width(4)) E (.D(Din), .en(decoder_1_out3), .Q(E_q), .clk(Clk));  // open: clr
  Register #(.width(4)) F (.D(Din), .en(decoder_1_out4), .Q(F_q), .clk(Clk));  // open: clr
  Register #(.width(4)) G (.D(Din), .en(decoder_1_out5), .Q(G_q), .clk(Clk));  // open: clr
  assign Dout = decoder_2_out0 ? B_q : 4'bz;  // Controlled_Buffer controlled_buffer_1
  assign Dout = decoder_2_out1 ? C_q : 4'bz;  // Controlled_Buffer controlled_buffer_2
  assign Dout = decoder_2_out2 ? D_q : 4'bz;  // Controlled_Buffer controlled_buffer_3
  assign Dout = decoder_2_out3 ? E_q : 4'bz;  // Controlled_Buffer controlled_buffer_4
  assign Dout = decoder_2_out4 ? F_q : 4'bz;  // Controlled_Buffer controlled_buffer_5
  assign Dout = decoder_2_out5 ? G_q : 4'bz;  // Controlled_Buffer controlled_buffer_6
  assign Dout = decoder_2_out6 ? 4'b1111 : 4'bz;  // Controlled_Buffer controlled_buffer_7
  Decoder #(.select(3), .enable("false")) decoder_2 (
    .out0(decoder_2_out0), .out1(decoder_2_out1), .out2(decoder_2_out2), .out3(decoder_2_out3),
    .out4(decoder_2_out4), .out5(decoder_2_out5), .out6(decoder_2_out6), .sel(Set));  // open: out7

  // Notes on the sheet:
  //   González Robles David Alejandro
endmodule

module ALU_T_4op2r (
  input  [3:0] ALUin,
  input  [1:0] WALU,
  input  CLK,
  input  [2:0] SetOp,
  output [3:0] ALUout
);

  wire decoder_1_out0, decoder_1_out1, decoder_2_out0, decoder_2_out1, decoder_2_out2, decoder_2_out3;
  wire [3:0] adder_1_out, and_1_out, or_1_out, T1_q, T2_q, xor_1_out;

  Decoder #(.select(2), .enable("false")) decoder_1 (
    .out0(decoder_1_out0), .out1(decoder_1_out1), .sel(WALU));  // open: out2, out3
  Register #(.width(4)) T1 (.D(ALUin), .en(decoder_1_out0), .Q(T1_q), .clk(CLK));  // open: clr
  Register #(.width(4)) T2 (.D(ALUin), .en(decoder_1_out1), .Q(T2_q), .clk(CLK));  // open: clr
  assign and_1_out = T1_q & T2_q;  // AND_Gate and_1, 4 bits wide
  assign or_1_out = T1_q | T2_q;  // OR_Gate or_1, 4 bits wide
  Adder #(.width(4)) adder_1 (.a(T1_q), .b(T2_q), .out(adder_1_out));  // open: cin, cout
  assign ALUout = decoder_2_out0 ? and_1_out : 4'bz;  // Controlled_Buffer controlled_buffer_1
  assign ALUout = decoder_2_out1 ? or_1_out : 4'bz;  // Controlled_Buffer controlled_buffer_2
  assign ALUout = decoder_2_out2 ? xor_1_out : 4'bz;  // Controlled_Buffer controlled_buffer_3
  assign xor_1_out = T1_q ^ T2_q;  // XOR_Gate xor_1, 4 bits wide
  assign ALUout = decoder_2_out3 ? adder_1_out : 4'bz;  // Controlled_Buffer controlled_buffer_4
  Decoder #(.select(3), .enable("false")) decoder_2 (
    .out0(decoder_2_out0), .out1(decoder_2_out1), .out2(decoder_2_out2), .out3(decoder_2_out3), .sel(SetOp));  // open: out4, out5, out6, out7

  // Notes on the sheet:
  //   González Robles David Alejandro
endmodule

// ALU
module ALU_T_4op1r (
  input  [3:0] Acin,
  input  [3:0] ALUin,
  input  WALU,
  input  CLK,
  input  [2:0] SetOp,
  output [3:0] ALUout
);

  wire decoder_1_out0, decoder_1_out1, decoder_1_out2, decoder_1_out3;
  wire [3:0] adder_1_out, and_1_out, or_1_out, T2_q, xor_1_out;

  Register #(.width(4)) T2 (.D(ALUin), .en(WALU), .Q(T2_q), .clk(CLK));  // open: clr
  assign and_1_out = Acin & T2_q;  // AND_Gate and_1, 4 bits wide
  assign or_1_out = Acin | T2_q;  // OR_Gate or_1, 4 bits wide
  assign xor_1_out = Acin ^ T2_q;  // XOR_Gate xor_1, 4 bits wide
  Adder #(.width(4)) adder_1 (.a(Acin), .b(T2_q), .out(adder_1_out));  // open: cin, cout
  assign ALUout = decoder_1_out0 ? and_1_out : 4'bz;  // Controlled_Buffer controlled_buffer_1
  assign ALUout = decoder_1_out1 ? or_1_out : 4'bz;  // Controlled_Buffer controlled_buffer_2
  assign ALUout = decoder_1_out2 ? xor_1_out : 4'bz;  // Controlled_Buffer controlled_buffer_3
  assign ALUout = decoder_1_out3 ? adder_1_out : 4'bz;  // Controlled_Buffer controlled_buffer_4
  Decoder #(.select(3), .enable("false")) decoder_1 (
    .out0(decoder_1_out0), .out1(decoder_1_out1), .out2(decoder_1_out2), .out3(decoder_1_out3), .sel(SetOp));  // open: out4, out5, out6, out7

  // Notes on the sheet:
  //   González Robles David Alejandro
endmodule

// Memoria
module Chips_de_memoria (
  input  [15:0] A,
  input  R_W,
  input  [3:0] DIN,
  input  CLK,
  output [3:0] DOUT
);

  wire decoder_1_out0, decoder_1_out1, decoder_1_out2, decoder_1_out3, decoder_1_out4, decoder_1_out5,
       decoder_1_out6, decoder_1_out7;

  Decoder #(.select(3), .enable("false")) decoder_1 (
    .out0(decoder_1_out0), .out1(decoder_1_out1), .out2(decoder_1_out2), .out3(decoder_1_out3),
    .out4(decoder_1_out4), .out5(decoder_1_out5), .out6(decoder_1_out6), .out7(decoder_1_out7), .sel(A[15:13]));
  RAM #(.addrWidth(13), .dataWidth(4), .bus("separate")) ram_1 (
    .addr(A[12:0]), .din(DIN), .data(DOUT), .sel(decoder_1_out0), .clk(CLK), .ld(R_W));  // open: str, clr
  RAM #(.addrWidth(13), .dataWidth(4), .bus("separate")) ram_2 (
    .addr(A[12:0]), .din(DIN), .data(DOUT), .sel(decoder_1_out1), .clk(CLK), .ld(R_W));  // open: str, clr
  RAM #(.addrWidth(13), .dataWidth(4), .bus("separate")) ram_3 (
    .addr(A[12:0]), .din(DIN), .data(DOUT), .sel(decoder_1_out2), .clk(CLK), .ld(R_W));  // open: str, clr
  RAM #(.addrWidth(13), .dataWidth(4), .bus("separate")) ram_4 (
    .addr(A[12:0]), .din(DIN), .data(DOUT), .sel(decoder_1_out3), .clk(CLK), .ld(R_W));  // open: str, clr
  RAM #(.addrWidth(13), .dataWidth(4), .bus("separate")) ram_5 (
    .addr(A[12:0]), .din(DIN), .data(DOUT), .sel(decoder_1_out4), .clk(CLK), .ld(R_W));  // open: str, clr
  RAM #(.addrWidth(13), .dataWidth(4), .bus("separate")) ram_6 (
    .addr(A[12:0]), .din(DIN), .data(DOUT), .sel(decoder_1_out5), .clk(CLK), .ld(R_W));  // open: str, clr
  RAM #(.addrWidth(13), .dataWidth(4), .bus("separate")) ram_7 (
    .addr(A[12:0]), .din(DIN), .data(DOUT), .sel(decoder_1_out6), .clk(CLK), .ld(R_W));  // open: str, clr
  RAM #(.addrWidth(13), .dataWidth(4), .bus("separate")) ram_8 (
    .addr(A[12:0]), .din(DIN), .data(DOUT), .sel(decoder_1_out7), .clk(CLK), .ld(R_W));  // open: str, clr

  // Notes on the sheet:
  //   González Robles David Alejandro   |   Bus de 16 bits. Chips de 8KB no paginada.
endmodule
