// Logisim project ARREGLO DE REGISTROS DE 4 BITS DE 2 REGISTROS.circ as structural Verilog: 1 circuit, main circuit main
module main (
  input  [3:0] Din,
  input  W,
  input  S,
  output [3:0] Dout
);

  wire CLK_out, not_1_out;
  wire [3:0] register_1_q, register_2_q;

  Clock CLK (.out(CLK_out));
  Register #(.width(4)) register_1 (.D(Din), .en(not_1_out), .Q(register_1_q), .clk(CLK_out));  // open: clr
  not not_1 (not_1_out, W);
  Register #(.width(4)) register_2 (.D(Din), .en(W), .Q(register_2_q), .clk(CLK_out));  // open: clr
  Multiplexer #(.width(4), .enable("false")) multiplexer_1 (
    .in0(register_1_q), .in1(register_2_q), .out(Dout), .sel(S));
endmodule
