// Logisim project ARRT y ALUT.circ as structural Verilog: 4 circuits, main circuit main
module main (
  input  Wac,
  input  [1:0] SetAc,
  input  [3:0] Data,
  input  [2:0] W,
  input  WALU,
  input  [2:0] SetAR,
  input  [2:0] SetOP,
  output [3:0] out_8,
  output [3:0] out_9
);

  wire clock_1_out;
  wire [3:0] multiplexer_1_out, register_1_q;

  Clock clock_1 (.out(clock_1_out));
  Multiplexer #(.select(2), .width(4), .enable("false")) multiplexer_1 (
    .in0(out_8), .in1(Data), .in2(out_9), .out(multiplexer_1_out), .sel(SetAc));  // open: in3
  ARR_T_4B arr_t_4b_1 (.Din(Data), .W(W), .Clk(clock_1_out), .Set(SetAR), .Dout(out_9));
  Register #(.width(4)) register_1 (.D(multiplexer_1_out), .en(Wac), .Q(register_1_q), .clk(clock_1_out));  // open: clr
  ALU_T_4op1r alu_t_4op1r_1 (
    .Acin(register_1_q), .ALUin(out_9), .WALU(WALU), .CLK(clock_1_out), .SetOp(SetOP), .ALUout(out_8));

  // Notes on the sheet:
  //   Equipo
  //   García Aguilar Rubén
  //   González Robles David Alejandro
  //   Lima Almaraz Javier Sayed
endmodule

module ARR_T_4B (
  input  [3:0] Din,
  input  Clk,
  input  [2:0] W,
  input  [2:0] Set,
  output [3:0] Dout
);

  wire decoder_1_out0, decoder_1_out1, decoder_1_out2, decoder_1_out3, decoder_1_out4, decoder_1_out5,
       decoder_2_out0, decoder_2_out1, decoder_2_out2, decoder_2_out3, decoder_2_out4, decoder_2_out5,
       decoder_2_out6;
  wire [3:0] B_q, C_q, D_q, E_q, F_q, G_q;

  Decoder #(.select(3), .enable("false")) decoder_1 (
    .out0(decoder_1_out0), .out1(decoder_1_out1), .out2(decoder_1_out2), .out3(decoder_1_out3),
    .out4(decoder_1_out4), .out5(decoder_1_out5), .sel(W));  // open: out6, out7
  Register #(.width(4)) B (.D(Din), .en(decoder_1_out0), .Q(B_q), .clk(Clk));  // open: clr
  Register #(.width(4)) C (.D(Din), .en(decoder_1_out1), .Q(C_q), .clk(Clk));  // open: clr
  Register #(.width(4)) D (.D(Din), .en(decoder_1_out2), .Q(D_q), .clk(Clk));  // open: clr
  Register #(.width(4)) E (.D(Din), .en(decoder_1_out3), .Q(E_q), .clk(Clk));  // open: clr
  Register #(.width(4)) F (.D(Din), .en(decoder_1_out4), .Q(F_q), .clk(Clk));  // open: clr
  Register #(.width(4)) G (.D(Din), .en(decoder_1_out5), .Q(G_q), .clk(Clk));  // open: clr
  assign Dout = decoder_2_out0 ? B_q : 4'bz;  // Controlled_Buffer controlled_buffer_1
  assign Dout = decoder_2_out1 ? C_q : 4'bz;  // Controlled_Buffer controlled_buffer_2
  assign Dout = decoder_2_out2 ? D_q : 4'bz;  // Controlled_Buffer controlled_buffer_3
  assign Dout = decoder_2_out3 ? E_q : 4'bz;  // Controlled_Buffer controlled_buffer_4
  assign Dout = decoder_2_out4 ? F_q : 4'bz;  // Controlled_Buffer controlled_buffer_5
  assign Dout = decoder_2_out5 ? G_q : 4'bz;  // Controlled_Buffer controlled_buffer_6
  assign Dout = decoder_2_out6 ? 4'b1111 : 4'bz;  // Controlled_Buffer controlled_buffer_7
  Decoder #(.select(3), .enable("false")) decoder_2 (
    .out0(decoder_2_out0), .out1(decoder_2_out1), .out2(decoder_2_out2), .out3(decoder_2_out3),
    .out4(decoder_2_out4), .out5(decoder_2_out5), .out6(decoder_2_out6), .sel(Set));  // open: out7

  // Notes on the sheet:
  //   Equipo
  //   García Aguilar Rubén
  //   Lima Almaraz Javier Sayed
  //   González Robles David Alejandro
endmodule

module ALU_T_4op2r (
  input  [3:0] ALUin,
  input  [1:0] WALU,
  input  CLK,
  input  [2:0] SetOp,
  output [3:0] ALUout
);

  wire decoder_1_out0, decoder_1_out1, decoder_2_out0, decoder_2_out1, decoder_2_out2, decoder_2_out3;
  wire [3:0] adder_1_out, and_1_out, or_1_out, T1_q, T2_q, xor_1_out;

  Decoder #(.select(2), .enable("false")) decoder_1 (
    .out0(decoder_1_out0), .out1(decoder_1_out1), .sel(WALU));  // open: out2, out3
  Register #(.width(4)) T1 (.D(ALUin), .en(decoder_1_out0), .Q(T1_q), .clk(CLK));  // open: clr
  Register #(.width(4)) T2 (.D(ALUin), .en(decoder_1_out1), .Q(T2_q), .clk(CLK));  // open: clr
  assign and_1_out = T1_q & T2_q;  // AND_Gate and_1, 4 bits wide
  assign or_1_out = T1_q | T2_q;  // OR_Gate or_1, 4 bits wide
  Adder #(.width(4)) adder_1 (.a(T1_q), .b(T2_q), .out(adder_1_out));  // open: cin, cout
  assign ALUout = decoder_2_out0 ? and_1_out : 4'bz;  // Controlled_Buffer controlled_buffer_1
  assign ALUout = decoder_2_out1 ? or_1_out : 4'bz;  // Controlled_Buffer controlled_buffer_2
  assign xor_1_out = T1_q ^ T2_q;  // XOR_Gate xor_1, 4 bits wide
  assign ALUout = decoder_2_out2 ? xor_1_out : 4'bz;  // Controlled_Buffer controlled_buffer_3
  assign ALUout = decoder_2_out3 ? adder_1_out : 4'bz;  // Controlled_Buffer controlled_buffer_4
  Decoder #(.select(3), .enable("false")) decoder_2 (
    .out0(decoder_2_out0), .out1(decoder_2_out1), .out2(decoder_2_out2), .out3(decoder_2_out3), .sel(SetOp));  // open: out4, out5, out6, out7

  // Notes on the sheet:
  //   Equipo
  //   García Aguilar Rubén
  //   Lima Almaraz Javier Sayed
  //   González Robles David Alejandro
endmodule

module ALU_T_4op1r (
  input  [3:0] Acin,
  input  [3:0] ALUin,
  input  WALU,
  input  CLK,
  input  [2:0] SetOp,
  output [3:0] ALUout
);

  wire decoder_1_out0, decoder_1_out1, decoder_1_out2, decoder_1_out3;
  wire [3:0] adder_1_out, and_1_out, or_1_out, T2_q, xor_1_out;

  Register #(.width(4)) T2 (.D(ALUin), .en(WALU), .Q(T2_q), .clk(CLK));  // open: clr
  assign and_1_out = Acin & T2_q;  // AND_Gate and_1, 4 bits wide
  assign or_1_out = Acin | T2_q;  // OR_Gate or_1, 4 bits wide
  assign xor_1_out = Acin ^ T2_q;  // XOR_Gate xor_1, 4 bits wide
  Adder #(.width(4)) adder_1 (.a(Acin), .b(T2_q), .out(adder_1_out));  // open: cin, cout
  assign ALUout = decoder_1_out0 ? and_1_out : 4'bz;  // Controlled_Buffer controlled_buffer_1
  assign ALUout = decoder_1_out1 ? or_1_out : 4'bz;  // Controlled_Buffer controlled_buffer_2
  assign ALUout = decoder_1_out2 ? xor_1_out : 4'bz;  // Controlled_Buffer controlled_buffer_3
  assign ALUout = decoder_1_out3 ? adder_1_out : 4'bz;  // Controlled_Buffer controlled_buffer_4
  Decoder #(.select(3), .enable("false")) decoder_1 (
    .out0(decoder_1_out0), .out1(decoder_1_out1), .out2(decoder_1_out2), .out3(decoder_1_out3), .sel(SetOp));  // open: out4, out5, out6, out7

  // Notes on the sheet:
  //   Equipo
  //   García Aguilar Rubén
  //   González Robles David Alejandro
  //   Lima Almaraz Javier Sayed
endmodule
