// Logisim project Bus 16b C32kb np.circ as structural Verilog: 1 circuit, main circuit main
module main (
  input  [15:0] A,
  input  R_W,
  input  [3:0] DIN,
  input  in_4,
  output [3:0] Dout
);

  wire decoder_1_out0, decoder_1_out1;

  Decoder #(.enable("false")) decoder_1 (.out0(decoder_1_out0), .out1(decoder_1_out1), .sel(A[15]));
  RAM #(.addrWidth(15), .dataWidth(4), .bus("separate")) ram_1 (
    .addr(A[14:0]), .din(DIN), .data(Dout), .sel(decoder_1_out0), .clk(in_4), .ld(R_W));  // open: str, clr
  RAM #(.addrWidth(15), .dataWidth(4), .bus("separate")) ram_2 (
    .addr(A[14:0]), .din(DIN), .data(Dout), .sel(decoder_1_out1), .clk(in_4), .ld(R_W));  // open: str, clr

  // Notes on the sheet:
  //   González Robles David Alejandro   |   Bus de 16 bits. Chips de 32KB no paginada.
endmodule
