// Logisim project Bus 16b C8kb np.circ as structural Verilog: 1 circuit, main circuit main
module main (
  input  [15:0] A,
  input  R_W,
  input  [3:0] DIN,
  input  in_4,
  output [3:0] DOUT
);

  wire decoder_1_out0, decoder_1_out1, decoder_1_out2, decoder_1_out3, decoder_1_out4, decoder_1_out5,
       decoder_1_out6, decoder_1_out7;

  Decoder #(.select(3), .enable("false")) decoder_1 (
    .out0(decoder_1_out0), .out1(decoder_1_out1), .out2(decoder_1_out2), .out3(decoder_1_out3),
    .out4(decoder_1_out4), .out5(decoder_1_out5), .out6(decoder_1_out6), .out7(decoder_1_out7), .sel(A[15:13]));
  RAM #(.addrWidth(13), .dataWidth(4), .bus("separate")) ram_1 (
    .addr(A[12:0]), .din(DIN), .data(DOUT), .sel(decoder_1_out0), .clk(in_4), .ld(R_W));  // open: str, clr
  RAM #(.addrWidth(13), .dataWidth(4), .bus("separate")) ram_2 (
    .addr(A[12:0]), .din(DIN), .data(DOUT), .sel(decoder_1_out1), .clk(in_4), .ld(R_W));  // open: str, clr
  RAM #(.addrWidth(13), .dataWidth(4), .bus("separate")) ram_3 (
    .addr(A[12:0]), .din(DIN), .data(DOUT), .sel(decoder_1_out2), .clk(in_4), .ld(R_W));  // open: str, clr
  RAM #(.addrWidth(13), .dataWidth(4), .bus("separate")) ram_4 (
    .addr(A[12:0]), .din(DIN), .data(DOUT), .sel(decoder_1_out3), .clk(in_4), .ld(R_W));  // open: str, clr
  RAM #(.addrWidth(13), .dataWidth(4), .bus("separate")) ram_5 (
    .addr(A[12:0]), .din(DIN), .data(DOUT), .sel(decoder_1_out4), .clk(in_4), .ld(R_W));  // open: str, clr
  RAM #(.addrWidth(13), .dataWidth(4), .bus("separate")) ram_6 (
    .addr(A[12:0]), .din(DIN), .data(DOUT), .sel(decoder_1_out5), .clk(in_4), .ld(R_W));  // open: str, clr
  RAM #(.addrWidth(13), .dataWidth(4), .bus("separate")) ram_7 (
    .addr(A[12:0]), .din(DIN), .data(DOUT), .sel(decoder_1_out6), .clk(in_4), .ld(R_W));  // open: str, clr
  RAM #(.addrWidth(13), .dataWidth(4), .bus("separate")) ram_8 (
    .addr(A[12:0]), .din(DIN), .data(DOUT), .sel(decoder_1_out7), .clk(in_4), .ld(R_W));  // open: str, clr

  // Notes on the sheet:
  //   González Robles David Alejandro   |   Bus de 16 bits. Chips de 8KB no paginada.
endmodule
