// Logisim project CONTADOR 3 BITS.circ as structural Verilog: 1 circuit, main circuit main
module main (
  input  [2:0] in_1,
  input  E,
  output out_3,
  output out_4,
  output out_5
);

  wire CLK_out, not_1_out, not_2_out, not_3_out;

  not not_1 (not_1_out, CLK_out);
  Clock CLK (.out(CLK_out));
  T_Flip_Flop t_ff_1 (.clk(not_1_out), .T(in_1[0]), .Q(out_5), .en(E));  // open: Qn, preset, reset
  not not_2 (not_2_out, out_5);
  T_Flip_Flop t_ff_2 (.clk(not_2_out), .T(in_1[1]), .Q(out_4), .en(E));  // open: Qn, preset, reset
  T_Flip_Flop t_ff_3 (.clk(not_3_out), .T(in_1[2]), .Q(out_3), .en(E));  // open: Qn, preset, reset
  not not_3 (not_3_out, out_4);

  // Notes on the sheet:
  //   Equipo
  //   García Aguilar Rubén
  //   Lima Almaraz Javier Sayed
  //   González Robles David Alejandro
endmodule
