// Logisim project Ejercicio 8 marzo.circ as structural Verilog: 1 circuit, main circuit main
module main (
  input  [1:0] in_1,
  input  W,
  output [3:0] Dout
);

  wire and_1_out, and_2_out, and_3_out, and_4_out, and_5_out, CLK_out, decoder_1_out0, decoder_1_out1,
       decoder_2_out0, decoder_2_out1, not_1_out;
  wire [3:0] controlled_buffer_1_out, register_1_q, register_2_q, register_3_q, register_4_q;

  Clock CLK (.out(CLK_out));
  Decoder #(.enable("false")) decoder_1 (.out0(decoder_1_out0), .out1(decoder_1_out1), .sel(in_1[1]));
  Register #(.width(4)) register_1 (
    .D(controlled_buffer_1_out), .en(and_1_out), .Q(register_1_q), .clk(and_3_out));  // open: clr
  and and_1 (and_1_out, decoder_2_out0, decoder_1_out0);
  Register #(.width(4)) register_2 (
    .D(controlled_buffer_1_out), .en(and_2_out), .Q(register_2_q), .clk(and_3_out));  // open: clr
  and and_2 (and_2_out, decoder_2_out0, decoder_1_out1);
  and and_3 (and_3_out, CLK_out, W);
  Decoder #(.enable("false")) decoder_2 (.out0(decoder_2_out0), .out1(decoder_2_out1), .sel(in_1[0]));
  and and_4 (and_4_out, decoder_2_out1, decoder_1_out0);
  and and_5 (and_5_out, decoder_2_out1, decoder_1_out1);
  Register #(.width(4)) register_3 (
    .D(controlled_buffer_1_out), .en(and_4_out), .Q(register_3_q), .clk(and_3_out));  // open: clr
  Register #(.width(4)) register_4 (
    .D(controlled_buffer_1_out), .en(and_5_out), .Q(register_4_q), .clk(and_3_out));  // open: clr
  not not_1 (not_1_out, W);
  assign controlled_buffer_1_out = W ? Dout : 4'bz;  // Controlled_Buffer controlled_buffer_1
  Multiplexer #(.select(2), .width(4)) multiplexer_1 (
    .in0(register_1_q), .in1(register_3_q), .in2(register_2_q), .in3(register_4_q), .out(Dout), .sel(in_1),
    .en(not_1_out));
endmodule
