// Logisim project FLIP FLOP D.circ as structural Verilog: 1 circuit, main circuit main
module main (
  input  D,
  output Q,
  output Q_2
);

  wire CLK_out, nand_1_out, nand_2_out, not_1_out;

  Clock CLK (.out(CLK_out));
  not not_1 (not_1_out, D);
  nand nand_1 (nand_1_out, D, CLK_out);
  nand nand_2 (nand_2_out, CLK_out, not_1_out);
  nand nand_3 (Q, nand_1_out, Q_2);
  nand nand_4 (Q_2, Q, nand_2_out);

  // Notes on the sheet:
  //   Equipo
  //   García Aguilar Rubén
  //   Lima Almaraz Javier Sayed
  //   FLIP FLOP D
  //   González Robles David Alejandro
endmodule
