// Logisim project FLIP FLOP SR.circ as structural Verilog: 1 circuit, main circuit main
module main (
  input  R,
  input  D,
  output Q,
  output Q_2
);

  wire and_1_out, and_2_out, CLK_out;

  Clock CLK (.out(CLK_out));
  and and_1 (and_1_out, R, CLK_out);
  and and_2 (and_2_out, CLK_out, D);
  nor nor_1 (Q, and_1_out, Q_2);
  nor nor_2 (Q_2, Q, and_2_out);

  // Notes on the sheet:
  //   FLIP FLOP SR
  //   Equipo
  //   García Aguilar Rubén
  //   Lima Almaraz Javier Sayed
  //   González Robles David Alejandro
endmodule
