// Logisim project LATCH SR.circ as structural Verilog: 1 circuit, main circuit main
module main (
  input  R,
  input  S,
  output Q,
  output Q_2
);

  nor nor_1 (Q, R, Q_2);
  nor nor_2 (Q_2, Q, S);

  // Notes on the sheet:
  //   Equipo
  //   García Aguilar Rubén
  //   Lima Almaraz Javier Sayed
  //   LATCH
  //   González Robles David Alejandro
endmodule
