// Logisim project MAIN CON ARREGLOS.circ as structural Verilog: 4 circuits, main circuit main
module main (
  input  [3:0] in_1,
  input  W,
  input  SE,
  output [3:0] out_4
);

  wire CLK_out;

  Clock CLK (.out(CLK_out));
  ARR_R_4B_2R arr_r_4b_2r_1 (.Din(in_1), .CLK(CLK_out), .W(W), .S(SE), .Dout(out_4));

  // Notes on the sheet:
  //   Equipo
  //   García Aguilar Rubén
  //   Lima Almaraz Javier Sayed
  //   González Robles David Alejandro
endmodule

module ARR_R_4B_2R (
  input  [3:0] Din,
  input  CLK,
  input  W,
  input  S,
  output [3:0] Dout
);

  wire not_1_out;
  wire [3:0] register_1_q, register_2_q;

  Register #(.width(4)) register_1 (.D(Din), .en(not_1_out), .Q(register_1_q), .clk(CLK));  // open: clr
  not not_1 (not_1_out, W);
  Register #(.width(4)) register_2 (.D(Din), .en(W), .Q(register_2_q), .clk(CLK));  // open: clr
  Multiplexer #(.width(4), .enable("false")) multiplexer_1 (
    .in0(register_1_q), .in1(register_2_q), .out(Dout), .sel(S));

  // Notes on the sheet:
  //   Equipo
  //   García Aguilar Rubén
  //   Lima Almaraz Javier Sayed
  //   González Robles David Alejandro
endmodule

module ARR_R_4B_4R (
  input  [3:0] Din,
  input  [1:0] S,
  input  [1:0] W,
  input  CLK,
  output [3:0] Dout
);

  wire and_1_out, and_2_out, and_3_out, and_4_out, not_1_out, not_2_out;
  wire [3:0] A_q, B_q, C_q, D_q;

  not not_1 (not_1_out, W[0]);
  not not_2 (not_2_out, W[1]);
  and and_1 (and_1_out, not_1_out, not_2_out);
  and and_2 (and_2_out, not_2_out, W[0]);
  and and_3 (and_3_out, not_1_out, W[1]);
  and and_4 (and_4_out, W[1], W[0]);
  Register #(.width(4)) A (.D(Din), .en(and_1_out), .Q(A_q), .clk(CLK));  // open: clr
  Register #(.width(4)) B (.D(Din), .en(and_2_out), .Q(B_q), .clk(CLK));  // open: clr
  Register #(.width(4)) C (.D(Din), .en(and_3_out), .Q(C_q), .clk(CLK));  // open: clr
  Register #(.width(4)) D (.D(Din), .en(and_4_out), .Q(D_q), .clk(CLK));  // open: clr
  Multiplexer #(.select(2), .width(4), .enable("false")) multiplexer_1 (
    .in0(A_q), .in1(B_q), .in2(C_q), .in3(D_q), .out(Dout), .sel(S));

  // Notes on the sheet:
  //   Equipo
  //   García Aguilar Rubén
  //   Lima Almaraz Javier Sayed
  //   González Robles David Alejandro
endmodule

module ARR_R_6B_7R (
  input  [5:0] DIn,
  input  [2:0] in_2,
  input  [2:0] in_3,
  output [5:0] out_4
);

  wire and_1_out, and_2_out, and_3_out, and_4_out, and_5_out, and_6_out, and_7_out, clock_1_out, not_1_out,
       not_2_out, not_3_out, not_4_out, not_5_out, not_6_out, not_7_out, not_8_out, not_9_out, not_10_out,
       not_11_out, not_12_out;
  wire [5:0] register_1_q, register_2_q, register_3_q, register_4_q, register_5_q, register_6_q, register_7_q;

  not not_1 (not_1_out, in_2[0]);
  not not_2 (not_2_out, in_2[0]);
  not not_3 (not_3_out, in_2[0]);
  not not_4 (not_4_out, in_2[0]);
  not not_5 (not_5_out, in_2[1]);
  and and_1 (and_1_out, not_1_out, not_5_out, not_6_out);
  not not_6 (not_6_out, in_2[2]);
  and and_2 (and_2_out, in_2[0], not_7_out, not_8_out);
  not not_7 (not_7_out, in_2[1]);
  not not_8 (not_8_out, in_2[2]);
  and and_3 (and_3_out, not_2_out, in_2[1], not_9_out);
  not not_9 (not_9_out, in_2[2]);
  not not_10 (not_10_out, in_2[1]);
  and and_4 (and_4_out, not_3_out, not_10_out, in_2[2]);
  and and_5 (and_5_out, not_4_out, in_2[1], in_2[2]);
  not not_11 (not_11_out, in_2[1]);
  and and_6 (and_6_out, in_2[0], not_11_out, in_2[2]);
  and and_7 (and_7_out, in_2[0], in_2[1], not_12_out);
  not not_12 (not_12_out, in_2[2]);
  Clock clock_1 (.out(clock_1_out));
  Register #(.width(6)) register_1 (.D(DIn), .en(and_1_out), .Q(register_1_q), .clk(clock_1_out));  // open: clr
  Register #(.width(6)) register_2 (.D(DIn), .en(and_2_out), .Q(register_2_q), .clk(clock_1_out));  // open: clr
  Register #(.width(6)) register_3 (.D(DIn), .en(and_3_out), .Q(register_3_q), .clk(clock_1_out));  // open: clr
  Register #(.width(6)) register_4 (.D(DIn), .en(and_4_out), .Q(register_4_q), .clk(clock_1_out));  // open: clr
  Register #(.width(6)) register_5 (.D(DIn), .en(and_5_out), .Q(register_5_q), .clk(clock_1_out));  // open: clr
  Register #(.width(6)) register_6 (.D(DIn), .en(and_6_out), .Q(register_6_q), .clk(clock_1_out));  // open: clr
  Register #(.width(6)) register_7 (.D(DIn), .en(and_7_out), .Q(register_7_q), .clk(clock_1_out));  // open: clr
  Multiplexer #(.select(3), .width(6), .enable("false")) multiplexer_1 (
    .in0(register_1_q), .in1(register_2_q), .in2(register_3_q), .in3(register_4_q), .in4(register_5_q),
    .in5(register_6_q), .in6(register_7_q), .out(out_4), .sel(in_3));  // open: in7

  // Notes on the sheet:
  //   Equipo
  //   García Aguilar Rubén
  //   González Robles David Alejandro
  //   Lima Almaraz Javier Sayed
endmodule
