// Logisim project REGISTRO 3 BITS.circ as structural Verilog: 1 circuit, main circuit main
module main (
  input  E,
  input  [2:0] in_2,
  output out_3,
  output out_4,
  output out_5
);

  wire CLK_out;

  Clock CLK (.out(CLK_out));
  D_Flip_Flop d_ff_1 (.clk(CLK_out), .D(in_2[2]), .Q(out_3), .en(E));  // open: Qn, preset, reset
  D_Flip_Flop d_ff_2 (.clk(CLK_out), .D(in_2[1]), .Q(out_4), .en(E));  // open: Qn, preset, reset
  D_Flip_Flop d_ff_3 (.clk(CLK_out), .D(in_2[0]), .Q(out_5), .en(E));  // open: Qn, preset, reset

  // Notes on the sheet:
  //   Equipo
  //   García Aguilar Rubén
  //   Lima Almaraz Javier Sayed
  //   REGISTRO
  //   González Robles David Alejandro
endmodule
