// Logisim project Repaso.circ as structural Verilog: 1 circuit, main circuit main
module main (
  input  R,
  input  S,
  input  D,
  input  E,
  input  R_2,
  input  D_2,
  input  D_3,
  output Q,
  output Q_2,
  output Q_3,
  output Q_4,
  output Q_5,
  output Q_6,
  output Q_7,
  output Q_8
);

  wire and_1_out, and_2_out, CLK_2_out, CLK_out, nand_1_out, nand_2_out, nand_3_out, nand_4_out, not_1_out;

  Clock CLK (.out(CLK_out));
  Clock CLK_2 (.out(CLK_2_out));
  nor nor_1 (Q, R, Q_2);
  nor nor_2 (Q_2, Q, S);
  nand nand_1 (nand_1_out, D, E);
  nand nand_2 (nand_2_out, nand_1_out, E);
  and and_1 (and_1_out, R_2, CLK_out);
  and and_2 (and_2_out, CLK_out, D_2);
  not not_1 (not_1_out, D_3);
  nand nand_3 (nand_3_out, D_3, CLK_2_out);
  nand nand_4 (nand_4_out, CLK_2_out, not_1_out);
  nand nand_5 (Q_3, nand_1_out, Q_4);
  nand nand_6 (Q_4, Q_3, nand_2_out);
  nor nor_3 (Q_5, and_1_out, Q_6);
  nor nor_4 (Q_6, Q_5, and_2_out);
  nand nand_7 (Q_7, nand_3_out, Q_8);
  nand nand_8 (Q_8, Q_7, nand_4_out);

  // Notes on the sheet:
  //   LATCH
  //   LATCH D
  //   FLIP FLOP D
  //   LATCH
  //   FLIP FLOP SR
endmodule
