// Logisim project SEMISUMADOR.circ as structural Verilog: 1 circuit, main circuit main
module main (
  input  A,
  input  B,
  output S,
  output COUT
);

  xor xor_1 (S, A, B);
  and and_1 (COUT, A, B);

  // Notes on the sheet:
  //   Equipo
  //   García Aguilar Rubén
  //   Lima Almaraz Javier Sayed
  //   Semisumador
  //   González Robles David Alejandro
endmodule
