// Logisim project SUMADOR COMPLETO PARA 2 BITS CON REGISTROS.circ as structural Verilog: 1 circuit, main circuit main
module main (
  input  [1:0] A,
  input  [1:0] B,
  input  Cin,
  input  [1:0] S,
  output out_5
);

  wire and_1_out, and_2_out, and_3_out, and_4_out, C0, xor_1_out, xor_2_out;
  wire [1:0] RA_q, RB_q, xor_3_out;

  Register #(.width(2)) RA (.D(A), .Q(RA_q));  // open: en, clk, clr
  Register #(.width(2)) RB (.D(B), .Q(RB_q));  // open: en, clk, clr
  xor xor_1 (xor_1_out, RA_q[0], RB_q[0]);
  and and_1 (and_1_out, RA_q[0], RB_q[0]);
  xor xor_2 (xor_2_out, RA_q[1], RB_q[1]);
  and and_2 (and_2_out, RA_q[1], RB_q[1]);
  xor xor_3 (xor_3_out[0], xor_1_out, Cin);
  or or_1 (C0, and_1_out, and_3_out);
  and and_3 (and_3_out, xor_1_out, Cin);
  xor xor_4 (xor_3_out[1], xor_2_out, C0);
  and and_4 (and_4_out, xor_2_out, C0);
  or or_2 (out_5, and_2_out, and_4_out);

  // Notes on the sheet:
  //   Equipo
  //   García Aguilar Rubén
  //   Lima Almaraz Javier Sayed
  //   González Robles David Alejandro
endmodule
