// Logisim project SUMADOR COMPLETO PARA DOS BITS.circ as structural Verilog: 1 circuit, main circuit main
module main (
  input  [1:0] A,
  input  [1:0] B,
  input  Cin,
  input  [2:0] S
);

  wire and_1_out, and_2_out, and_3_out, and_4_out, C0, xor_1_out, xor_2_out;
  wire [2:0] xor_3_out;

  xor xor_1 (xor_1_out, A[0], B[0]);
  and and_1 (and_1_out, A[0], B[0]);
  xor xor_2 (xor_2_out, A[1], B[1]);
  and and_2 (and_2_out, A[1], B[1]);
  and and_3 (and_3_out, xor_1_out, Cin);
  and and_4 (and_4_out, xor_2_out, C0);
  xor xor_3 (xor_3_out[0], xor_1_out, Cin);
  or or_1 (C0, and_1_out, and_3_out);
  xor xor_4 (xor_3_out[1], xor_2_out, C0);
  or or_2 (xor_3_out[2], and_2_out, and_4_out);

  // Notes on the sheet:
  //   Equipo
  //   García Aguilar Rubén
  //   Lima Almaraz Javier Sayed
  //   González Robles David Alejandro
endmodule
