// Logisim project espera.circ as structural Verilog: 1 circuit, main circuit main
module main (
  input  [16:0] A,
  input  R_W,
  input  [3:0] DIN,
  output [3:0] Dout
);

  Decoder #(.select(4), .enable("false")) decoder_1 ();  // open: out0, out1, out2, out3, out4, out5, out6, out7, out8, out9, out10, out11, out12, out13, out14, out15, sel
  Decoder #(.select(3), .enable("false")) decoder_2 ();  // open: out0, out1, out2, out3, out4, out5, out6, out7, sel
  RAM #(.dataWidth(4)) ram_1 ();  // open: addr, data, sel, clk, ld, clr
  RAM #(.dataWidth(4)) ram_2 ();  // open: addr, data, sel, clk, ld, clr
  RAM #(.dataWidth(4)) ram_3 ();  // open: addr, data, sel, clk, ld, clr
  RAM #(.dataWidth(4)) ram_4 ();  // open: addr, data, sel, clk, ld, clr
  RAM #(.dataWidth(4)) ram_5 ();  // open: addr, data, sel, clk, ld, clr
  RAM #(.dataWidth(4)) ram_6 ();  // open: addr, data, sel, clk, ld, clr
  RAM #(.dataWidth(4)) ram_7 ();  // open: addr, data, sel, clk, ld, clr
  RAM #(.dataWidth(4)) ram_8 ();  // open: addr, data, sel, clk, ld, clr
  RAM #(.dataWidth(4)) ram_9 ();  // open: addr, data, sel, clk, ld, clr
  RAM #(.dataWidth(4)) ram_10 ();  // open: addr, data, sel, clk, ld, clr
  RAM #(.dataWidth(4)) ram_11 ();  // open: addr, data, sel, clk, ld, clr
  RAM #(.dataWidth(4)) ram_12 ();  // open: addr, data, sel, clk, ld, clr
  // Pins of 16 and 17 bits meet at A

  // Notes on the sheet:
  //   González Robles David Alejandro   |   Bus de 17 bits. Chips de 8KB y 4KB paginada. (ultimos 32 KB repartidos en chips de 4KB
endmodule
